# Fritzing sketch esp_lcd_hx711 (saved by Fritzing 0.9.3b)
circuit board: 13.4302cm x 8.69951cm
breadboards: 1

parts:
  Componente2 = HX711 Weighing Sensor Module
  J1 = Piezo Speaker
  U2 = ESP8266 NodeMCU LoLin module
  U1 = LCD-16X2 [package=lcd-16x2]
  LCM1602_IIC1 = LCM1602 IIC [part_number="LCM1602 IIC" chip_label="LCM1602 IIC" package="DIP (Dual Inline) [THT]"]

nets:
  GND: Componente2.GND, J1.pin1, U2.GND, LCM1602_IIC1.GND
  N1: Componente2.DO/RX, U2.D6
  N2: Componente2.CK/TX, U2.D7
  N3: J1.pin2, U2.D5
  N4: U2.D1, LCM1602_IIC1.SCL
  N5: U2.D2, LCM1602_IIC1.SDA
  3V3: U2.3V3, LCM1602_IIC1.VCC
  VSS: U1.VSS, LCM1602_IIC1.VSS
  VDD: U1.VDD, LCM1602_IIC1.VDD
  N6: U1.VO, LCM1602_IIC1.V0
  N7: U1.RS, LCM1602_IIC1.RS
  N8: U1.R_W, LCM1602_IIC1.RW
  N9: U1.E, LCM1602_IIC1.E
  N10: U1.DB0, LCM1602_IIC1.D0
  N11: U1.DB1, LCM1602_IIC1.D1
  N12: U1.DB2, LCM1602_IIC1.D2
  N13: U1.DB3, LCM1602_IIC1.D3
  N14: U1.DB4, LCM1602_IIC1.D4
  N15: U1.DB5, LCM1602_IIC1.D5
  N16: U1.DB6, LCM1602_IIC1.D6
  N17: U1.DB7, LCM1602_IIC1.D7
  N18: U1.A, LCM1602_IIC1.A
  N19: U1.K, LCM1602_IIC1.K
  N20: LCM1602_IIC1.LED_A, LCM1602_IIC1.LED_B

custom parts:
  ESP8266 NodeMCU LoLin module: ESP8266 based NodeMCU
  LCM1602 IIC: I2C-Module to use a 1602 or 2004 LCD on with the wire.h libory Serial LCD Modul
